# Fritzing sketch Diagram (saved by Fritzing 0.9.3b)

parts:
  Part1 = Arduino Uno (Rev3)
  LCM1602_IIC2 = LCM1602 IIC [part_number="LCM1602 IIC" chip_label="LCM1602 IIC" package="DIP (Dual Inline) [THT]"]
  LCD = LCD-16X2 [package=lcd-16x2_nosilk]
  RTC = RTC_DS1302_module
  KY-3 = Keyes Relay [package=THT]
  Buzzer = Piezo Speaker
  IR1 = TSOP312.., 314.. [package=THT]
  BC548 = NPN-Transistor [package="TO92 [THT]"]
  R1 = Resistor [tolerance=±5% resistance=220 package="0805 [SMD]"]
  Battery = BC9VPC [package=bc9vpc]
  LED = smd LED [color="Green (570nm)" package="1206 [SMD]"]  # not connected
  R2 = Resistor [tolerance=±5% resistance=220 package="0805 [SMD]"]

nets:
  N1: Part1.A4/SDA, LCM1602_IIC2.SDA
  N2: Part1.A5/SCL, LCM1602_IIC2.SCL
  N3: Part1.D8, RTC.RST
  N4: Part1.D9_PWM, RTC.DAT
  N5: Part1.D10_PWM/SS, RTC.CLK
  N6: Part1.D11_PWM/MOSI, IR1.Data
  GND: Part1.GND, LCM1602_IIC2.GND, RTC.GND, Buzzer.pin1
  N7: Part1.D4, BC548.B
  N8: Part1.D5_PWM, RTC.VCC, Buzzer.pin2
  5V: Part1.5V, LCM1602_IIC2.VCC
  VSS: LCM1602_IIC2.VSS, LCD.VSS
  VDD: LCM1602_IIC2.VDD, LCD.VDD
  N9: LCM1602_IIC2.V0, LCD.VO
  N10: LCM1602_IIC2.RS, LCD.RS
  N11: LCM1602_IIC2.RW, LCD.R_W
  N12: LCM1602_IIC2.E, LCD.E
  N13: LCM1602_IIC2.D0, LCD.DB0
  N14: LCM1602_IIC2.D1, LCD.DB1
  N15: LCM1602_IIC2.D2, LCD.DB2
  N16: LCM1602_IIC2.D3, LCD.DB3
  N17: LCM1602_IIC2.D4, LCD.DB4
  N18: LCM1602_IIC2.D5, LCD.DB5
  N19: LCM1602_IIC2.D6, LCD.DB6
  N20: LCM1602_IIC2.D7, LCD.DB7
  N21: LCM1602_IIC2.A, LCD.A
  N22: LCM1602_IIC2.K, LCD.K
  N23: KY-3.signal, R1.Pin_1
  N24: KY-3.ground, BC548.C
  N25: KY-3.C, Battery.V-
  N26: KY-3.NO, R2.Pin_0

custom parts:
  LCM1602 IIC: I2C-Module to use a 1602 or 2004 LCD on with the wire.h libory Serial LCD Modul
  RTC_DS1302_module: Arduino module DS1302 SPI Real Time Clock
  Keyes Relay: The Keyes 5V relay module is suitable for SCM development, home appliance control. It uses a 5V~12V TIL control signal which can control DC / AC signal.
